// Logisim project lab10.circ as structural Verilog: 4 circuits, main circuit main
module main (
);

  wire clock_1_out, decoder_1_dstmux, fields_1_register, not_1_out;
  wire [1:0] decoder_1_alu_op;
  wire [3:0] fields_1_opcode;
  wire [7:0] A_q, adder_1_out, alu_1_output, B_q, fields_1_immediate, multiplexer_1_out, PC_q;
  wire [15:0] rom_1_data;

  Register PC (.D(adder_1_out), .en(1'b1), .Q(PC_q), .clk(clock_1_out));  // open: clr
  Adder adder_1 (.a(PC_q), .b(8'h1), .out(adder_1_out));  // open: cin, cout
  Clock clock_1 (.out(clock_1_out));
  ROM #(.dataWidth(16)) rom_1 (.addr(PC_q), .data(rom_1_data), .sel(1'b1));
  Fields fields_1 (
    .Input(rom_1_data), .Immediate(fields_1_immediate), .Register(fields_1_register), .Opcode(fields_1_opcode));
  not not_1 (not_1_out, fields_1_register);
  Decoder decoder_1 (.Opcode(fields_1_opcode), .ALU_OP(decoder_1_alu_op), .DstMux(decoder_1_dstmux));
  Register A (.D(multiplexer_1_out), .en(not_1_out), .Q(A_q), .clk(clock_1_out));  // open: clr
  Register B (.D(multiplexer_1_out), .en(fields_1_register), .Q(B_q), .clk(clock_1_out));  // open: clr
  ALU alu_1 (.A(A_q), .B(B_q), .Operation(decoder_1_alu_op), .Output(alu_1_output));
  Multiplexer #(.width(8)) multiplexer_1 (
    .in0(alu_1_output), .in1(fields_1_immediate), .out(multiplexer_1_out), .sel(decoder_1_dstmux));  // open: en

  // Notes on the sheet:
  //   contents of rom_1 (hex, n*v repeats v):
  //   1 802 2800 3000 4800 5800
endmodule

module ALU (
  input  [1:0] Operation,
  input  [7:0] A,
  input  [7:0] B,
  output [7:0] Output
);

  wire [7:0] adder_1_out, and_1_out, or_1_out, subtractor_1_out;

  assign and_1_out = A & B;  // AND_Gate and_1, 8 bits wide
  assign or_1_out = A | B;  // OR_Gate or_1, 8 bits wide
  Adder adder_1 (.a(A), .b(B), .out(adder_1_out));  // open: cin, cout
  Subtractor subtractor_1 (.a(A), .b(B), .out(subtractor_1_out));  // open: bin, bout
  Multiplexer #(.select(2), .width(8)) multiplexer_1 (
    .in0(adder_1_out), .in1(subtractor_1_out), .in2(or_1_out), .in3(and_1_out), .out(Output), .sel(Operation));  // open: en
endmodule

module Fields (
  input  [15:0] Input,
  output [7:0] Immediate,
  output Register,
  output [3:0] Opcode
);


  assign Immediate = Input[7:0];
  assign Opcode = Input[15:12];
  assign Register = Input[11];
endmodule

module Decoder (
  input  [3:0] Opcode,
  output [1:0] ALU_OP,
  output DstMux
);

  wire not_2_out;

  not not_1 (ALU_OP[1], Opcode[1]);
  not not_2 (not_2_out, Opcode[2]);
  and and_1 (DstMux, not_2_out, ALU_OP[1]);

  assign ALU_OP[0] = Opcode[0];
endmodule
