// Logisim project lab09.circ as structural Verilog: 1 circuit, main circuit main
module main (
  input  WriteEnable,
  input  [2:0] Read_Register_1,
  input  [2:0] write_Register,
  input  [2:0] Read_Register_2,
  input  [31:0] Write_Data,
  output [31:0] ReadReg_1_value,
  output [31:0] ReadReg_2_value
);

  wire and_1_out, and_2_out, and_3_out, and_4_out, and_5_out, and_6_out, and_7_out, and_8_out, clock_1_out,
       decoder_1_out0, decoder_1_out1, decoder_1_out2, decoder_1_out3, decoder_1_out4, decoder_1_out5,
       decoder_1_out6, decoder_1_out7;
  wire [31:0] Register1_q, Register2_q, Register3_q, Register4_q, Register5_q, Register6_q, Register7_q,
       Register8_q;

  Decoder #(.select(3)) decoder_1 (
    .out0(decoder_1_out0), .out1(decoder_1_out1), .out2(decoder_1_out2), .out3(decoder_1_out3),
    .out4(decoder_1_out4), .out5(decoder_1_out5), .out6(decoder_1_out6), .out7(decoder_1_out7),
    .sel(write_Register));  // open: en
  and and_1 (and_1_out, WriteEnable, decoder_1_out0);
  and and_2 (and_2_out, decoder_1_out1, WriteEnable);
  and and_3 (and_3_out, decoder_1_out2, WriteEnable);
  and and_4 (and_4_out, decoder_1_out3, WriteEnable);
  and and_5 (and_5_out, decoder_1_out4, WriteEnable);
  and and_6 (and_6_out, decoder_1_out5, WriteEnable);
  and and_7 (and_7_out, decoder_1_out6, WriteEnable);
  and and_8 (and_8_out, decoder_1_out7, WriteEnable);
  Clock clock_1 (.out(clock_1_out));
  Register #(.width(32)) Register1 (.D(Write_Data), .en(and_1_out), .Q(Register1_q), .clk(clock_1_out));  // open: clr
  Register #(.width(32)) Register2 (.D(Write_Data), .en(and_2_out), .Q(Register2_q), .clk(clock_1_out));  // open: clr
  Register #(.width(32)) Register3 (.D(Write_Data), .en(and_3_out), .Q(Register3_q), .clk(clock_1_out));  // open: clr
  Register #(.width(32)) Register4 (.D(Write_Data), .en(and_4_out), .Q(Register4_q), .clk(clock_1_out));  // open: clr
  Register #(.width(32)) Register5 (.D(Write_Data), .en(and_5_out), .Q(Register5_q), .clk(clock_1_out));  // open: clr
  Register #(.width(32)) Register6 (.D(Write_Data), .en(and_6_out), .Q(Register6_q), .clk(clock_1_out));  // open: clr
  Register #(.width(32)) Register7 (.D(Write_Data), .en(and_7_out), .Q(Register7_q));  // open: clk, clr
  Register #(.width(32)) Register8 (.D(Write_Data), .en(and_8_out), .Q(Register8_q), .clk(clock_1_out));  // open: clr
  Multiplexer #(.select(3), .width(32)) multiplexer_1 (
    .in0(Register1_q), .in1(Register2_q), .in2(Register3_q), .in3(Register4_q), .in4(Register5_q),
    .in5(Register6_q), .in6(Register7_q), .in7(Register8_q), .out(ReadReg_1_value), .sel(Read_Register_1));  // open: en
  Multiplexer #(.select(3), .width(32)) multiplexer_2 (
    .in0(Register1_q), .in1(Register2_q), .in2(Register3_q), .in3(Register4_q), .in4(Register5_q),
    .in5(Register6_q), .in6(Register7_q), .in7(Register8_q), .out(ReadReg_2_value), .sel(Read_Register_2));  // open: en
endmodule
