// Logisim project CPU.circ as structural Verilog
module Register_File (
  input  Write_Enable,
  input  [4:0] Read_Register_1,
  input  [4:0] Read_Register_2,
  input  [4:0] Write_Register,
  input  [31:0] Write_Data,
  output [31:0] ReadReg_1_Value,
  output [31:0] ReadReg_2_Value
);

  wire and_1_out, and_2_out, and_3_out, and_4_out, and_5_out, and_6_out, and_7_out, and_8_out, and_9_out,
       and_10_out, and_11_out, and_12_out, and_13_out, and_14_out, and_15_out, and_16_out, and_17_out,
       and_18_out, and_19_out, and_20_out, and_21_out, and_22_out, and_23_out, and_24_out, and_25_out,
       and_26_out, and_27_out, and_28_out, and_29_out, and_30_out, and_31_out, and_32_out, clock_1_out,
       decoder_1_out0, decoder_1_out1, decoder_1_out2, decoder_1_out3, decoder_1_out4, decoder_1_out5,
       decoder_1_out6, decoder_1_out7, decoder_1_out8, decoder_1_out9, decoder_1_out10, decoder_1_out11,
       decoder_1_out12, decoder_1_out13, decoder_1_out14, decoder_1_out15, decoder_1_out16, decoder_1_out17,
       decoder_1_out18, decoder_1_out19, decoder_1_out20, decoder_1_out21, decoder_1_out22, decoder_1_out23,
       decoder_1_out24, decoder_1_out25, decoder_1_out26, decoder_1_out27, decoder_1_out28, decoder_1_out29,
       decoder_1_out30, decoder_1_out31;
  wire [31:0] Register1_q, Register2_q, Register3_q, Register4_q, Register5_q, Register6_q, Register7_q,
       Register8_q, Register9_q, Register10_q, Register11_q, Register12_q, Register13_q, Register14_q,
       Register15_q, Register16_q, Register17_q, Register18_q, Register19_q, Register20_q, Register21_q,
       Register22_q, Register23_q, Register24_q, Register25_q, Register26_q, Register27_q, Register28_q,
       Register29_q, Register30_q, Register31_q, Register32_q;

  Decoder #(.select(5)) decoder_1 (
    .out0(decoder_1_out0), .out1(decoder_1_out1), .out2(decoder_1_out2), .out3(decoder_1_out3),
    .out4(decoder_1_out4), .out5(decoder_1_out5), .out6(decoder_1_out6), .out7(decoder_1_out7),
    .out8(decoder_1_out8), .out9(decoder_1_out9), .out10(decoder_1_out10), .out11(decoder_1_out11),
    .out12(decoder_1_out12), .out13(decoder_1_out13), .out14(decoder_1_out14), .out15(decoder_1_out15),
    .out16(decoder_1_out16), .out17(decoder_1_out17), .out18(decoder_1_out18), .out19(decoder_1_out19),
    .out20(decoder_1_out20), .out21(decoder_1_out21), .out22(decoder_1_out22), .out23(decoder_1_out23),
    .out24(decoder_1_out24), .out25(decoder_1_out25), .out26(decoder_1_out26), .out27(decoder_1_out27),
    .out28(decoder_1_out28), .out29(decoder_1_out29), .out30(decoder_1_out30), .out31(decoder_1_out31),
    .sel(Write_Register));  // open: en
  and and_1 (and_1_out, Write_Enable, decoder_1_out0);
  and and_2 (and_2_out, Write_Enable, decoder_1_out1);
  and and_3 (and_3_out, Write_Enable, decoder_1_out2);
  and and_4 (and_4_out, Write_Enable, decoder_1_out3);
  and and_5 (and_5_out, Write_Enable, decoder_1_out4);
  and and_6 (and_6_out, Write_Enable, decoder_1_out5);
  and and_7 (and_7_out, Write_Enable, decoder_1_out6);
  and and_8 (and_8_out, Write_Enable, decoder_1_out7);
  and and_9 (and_9_out, Write_Enable, decoder_1_out8);
  and and_10 (and_10_out, Write_Enable, decoder_1_out9);
  and and_11 (and_11_out, Write_Enable, decoder_1_out10);
  and and_12 (and_12_out, Write_Enable, decoder_1_out11);
  and and_13 (and_13_out, Write_Enable, decoder_1_out12);
  and and_14 (and_14_out, Write_Enable, decoder_1_out13);
  and and_15 (and_15_out, Write_Enable, decoder_1_out14);
  and and_16 (and_16_out, Write_Enable, decoder_1_out15);
  and and_17 (and_17_out, Write_Enable, decoder_1_out16);
  and and_18 (and_18_out, Write_Enable, decoder_1_out17);
  and and_19 (and_19_out, Write_Enable, decoder_1_out18);
  and and_20 (and_20_out, Write_Enable, decoder_1_out19);
  and and_21 (and_21_out, Write_Enable, decoder_1_out20);
  and and_22 (and_22_out, Write_Enable, decoder_1_out21);
  and and_23 (and_23_out, Write_Enable, decoder_1_out22);
  and and_24 (and_24_out, Write_Enable, decoder_1_out23);
  and and_25 (and_25_out, Write_Enable, decoder_1_out24);
  and and_26 (and_26_out, Write_Enable, decoder_1_out25);
  and and_27 (and_27_out, Write_Enable, decoder_1_out26);
  and and_28 (and_28_out, Write_Enable, decoder_1_out27);
  and and_29 (and_29_out, Write_Enable, decoder_1_out28);
  and and_30 (and_30_out, Write_Enable, decoder_1_out29);
  and and_31 (and_31_out, Write_Enable, decoder_1_out30);
  and and_32 (and_32_out, Write_Enable, decoder_1_out31);
  Register #(.width(32)) Register1 (.D(Write_Data), .en(and_1_out), .Q(Register1_q), .clk(clock_1_out));  // open: clr
  Register #(.width(32)) Register2 (.D(Write_Data), .en(and_2_out), .Q(Register2_q), .clk(clock_1_out));  // open: clr
  Register #(.width(32)) Register3 (.D(Write_Data), .en(and_3_out), .Q(Register3_q), .clk(clock_1_out));  // open: clr
  Register #(.width(32)) Register4 (.D(Write_Data), .en(and_4_out), .Q(Register4_q), .clk(clock_1_out));  // open: clr
  Register #(.width(32)) Register5 (.D(Write_Data), .en(and_5_out), .Q(Register5_q), .clk(clock_1_out));  // open: clr
  Register #(.width(32)) Register6 (.D(Write_Data), .en(and_6_out), .Q(Register6_q), .clk(clock_1_out));  // open: clr
  Register #(.width(32)) Register7 (.D(Write_Data), .en(and_7_out), .Q(Register7_q), .clk(clock_1_out));  // open: clr
  Register #(.width(32)) Register8 (.D(Write_Data), .en(and_8_out), .Q(Register8_q), .clk(clock_1_out));  // open: clr
  Register #(.width(32)) Register9 (.D(Write_Data), .en(and_9_out), .Q(Register9_q), .clk(clock_1_out));  // open: clr
  Register #(.width(32)) Register10 (
    .D(Write_Data), .en(and_10_out), .Q(Register10_q), .clk(clock_1_out));  // open: clr
  Register #(.width(32)) Register11 (
    .D(Write_Data), .en(and_11_out), .Q(Register11_q), .clk(clock_1_out));  // open: clr
  Register #(.width(32)) Register12 (
    .D(Write_Data), .en(and_12_out), .Q(Register12_q), .clk(clock_1_out));  // open: clr
  Register #(.width(32)) Register13 (
    .D(Write_Data), .en(and_13_out), .Q(Register13_q), .clk(clock_1_out));  // open: clr
  Register #(.width(32)) Register14 (
    .D(Write_Data), .en(and_14_out), .Q(Register14_q), .clk(clock_1_out));  // open: clr
  Register #(.width(32)) Register15 (
    .D(Write_Data), .en(and_15_out), .Q(Register15_q), .clk(clock_1_out));  // open: clr
  Register #(.width(32)) Register16 (
    .D(Write_Data), .en(and_16_out), .Q(Register16_q), .clk(clock_1_out));  // open: clr
  Register #(.width(32)) Register17 (
    .D(Write_Data), .en(and_17_out), .Q(Register17_q), .clk(clock_1_out));  // open: clr
  Register #(.width(32)) Register18 (
    .D(Write_Data), .en(and_18_out), .Q(Register18_q), .clk(clock_1_out));  // open: clr
  Register #(.width(32)) Register19 (
    .D(Write_Data), .en(and_19_out), .Q(Register19_q), .clk(clock_1_out));  // open: clr
  Register #(.width(32)) Register20 (
    .D(Write_Data), .en(and_20_out), .Q(Register20_q), .clk(clock_1_out));  // open: clr
  Register #(.width(32)) Register21 (
    .D(Write_Data), .en(and_21_out), .Q(Register21_q), .clk(clock_1_out));  // open: clr
  Register #(.width(32)) Register22 (
    .D(Write_Data), .en(and_22_out), .Q(Register22_q), .clk(clock_1_out));  // open: clr
  Register #(.width(32)) Register23 (
    .D(Write_Data), .en(and_23_out), .Q(Register23_q), .clk(clock_1_out));  // open: clr
  Register #(.width(32)) Register24 (
    .D(Write_Data), .en(and_24_out), .Q(Register24_q), .clk(clock_1_out));  // open: clr
  Register #(.width(32)) Register25 (
    .D(Write_Data), .en(and_25_out), .Q(Register25_q), .clk(clock_1_out));  // open: clr
  Register #(.width(32)) Register26 (
    .D(Write_Data), .en(and_26_out), .Q(Register26_q), .clk(clock_1_out));  // open: clr
  Register #(.width(32)) Register27 (
    .D(Write_Data), .en(and_27_out), .Q(Register27_q), .clk(clock_1_out));  // open: clr
  Register #(.width(32)) Register28 (
    .D(Write_Data), .en(and_28_out), .Q(Register28_q), .clk(clock_1_out));  // open: clr
  Register #(.width(32)) Register29 (
    .D(Write_Data), .en(and_29_out), .Q(Register29_q), .clk(clock_1_out));  // open: clr
  Register #(.width(32)) Register30 (
    .D(Write_Data), .en(and_30_out), .Q(Register30_q), .clk(clock_1_out));  // open: clr
  Register #(.width(32)) Register31 (
    .D(Write_Data), .en(and_31_out), .Q(Register31_q), .clk(clock_1_out));  // open: clr
  Register #(.width(32)) Register32 (
    .D(Write_Data), .en(and_32_out), .Q(Register32_q), .clk(clock_1_out));  // open: clr
  Clock clock_1 (.out(clock_1_out));
  Multiplexer #(.select(5), .width(32)) multiplexer_1 (
    .in0(Register1_q), .in1(Register2_q), .in2(Register3_q), .in3(Register4_q), .in4(Register5_q),
    .in5(Register6_q), .in6(Register7_q), .in7(Register8_q), .in8(Register9_q), .in9(Register10_q),
    .in10(Register11_q), .in11(Register12_q), .in12(Register13_q), .in13(Register14_q), .in14(Register15_q),
    .in15(Register16_q), .in16(Register17_q), .in17(Register18_q), .in18(Register19_q), .in19(Register20_q),
    .in20(Register21_q), .in21(Register22_q), .in22(Register23_q), .in23(Register24_q), .in24(Register25_q),
    .in25(Register26_q), .in26(Register27_q), .in27(Register28_q), .in28(Register29_q), .in29(Register30_q),
    .in30(Register31_q), .in31(Register32_q), .out(ReadReg_1_Value), .sel(Read_Register_1));  // open: en
  Multiplexer #(.select(5), .width(32)) multiplexer_2 (
    .in0(Register1_q), .in1(Register2_q), .in2(Register3_q), .in3(Register4_q), .in4(Register5_q),
    .in5(Register6_q), .in6(Register7_q), .in7(Register8_q), .in8(Register9_q), .in9(Register10_q),
    .in10(Register11_q), .in11(Register12_q), .in12(Register13_q), .in13(Register14_q), .in14(Register15_q),
    .in15(Register16_q), .in16(Register17_q), .in17(Register18_q), .in18(Register19_q), .in19(Register20_q),
    .in20(Register21_q), .in21(Register22_q), .in22(Register23_q), .in23(Register24_q), .in24(Register25_q),
    .in25(Register26_q), .in26(Register27_q), .in27(Register28_q), .in28(Register29_q), .in29(Register30_q),
    .in30(Register31_q), .in31(Register32_q), .out(ReadReg_2_Value), .sel(Read_Register_2));  // open: en
endmodule

module Test (
  input  Write_Enable,
  input  [4:0] Read_1,
  input  [4:0] Read_2,
  input  [4:0] Write,
  input  Binvert,
  input  [31:0] Write_Data,
  input  [1:0] Operation,
  input  Ainvert,
  input  [31:0] Write_Data_2,
  output [31:0] ReadReg_1_Value,
  output [31:0] ReadReg_2_Value,
  output [31:0] ReadReg_2_Value_2,
  output Zero
);

  Register_File register_file_1 (
    .Read_Register_1(Read_1), .Read_Register_2(Read_2), .Write_Register(Write), .Write_Data(Write_Data),
    .Write_Enable(Write_Enable), .ReadReg_1_Value(ReadReg_1_Value), .ReadReg_2_Value(ReadReg_2_Value));
  ALU alu_1 (
    .a(Write_Data), .b(Write_Data_2), .Ainvert(Ainvert), .Binvert(Binvert), .CarryIn(Binvert),
    .Operation(Operation), .Result(ReadReg_2_Value_2), .CarryOut(Zero));  // open: Zero
endmodule

module ALU (
  input  Ainvert,
  input  Binvert,
  input  CarryIn,
  input  [1:0] Operation,
  input  [31:0] a,
  input  [31:0] b,
  output [31:0] Result,
  output CarryOut,
  output Zero
);

  wire [31:0] adder_1_out, and_1_out, multiplexer_1_out, multiplexer_2_out, not_1_out, not_2_out, or_1_out;

  assign not_1_out = ~a;  // NOT_Gate not_1, 32 bits wide
  assign not_2_out = ~b;  // NOT_Gate not_2, 32 bits wide
  Multiplexer #(.width(32)) multiplexer_1 (
    .in0(a), .in1(not_1_out), .out(multiplexer_1_out), .sel(Ainvert));  // open: en
  Multiplexer #(.width(32)) multiplexer_2 (
    .in0(b), .in1(not_2_out), .out(multiplexer_2_out), .sel(Binvert));  // open: en
  assign and_1_out = multiplexer_1_out & multiplexer_2_out;  // AND_Gate and_1, 32 bits wide
  assign or_1_out = multiplexer_1_out | multiplexer_2_out;  // OR_Gate or_1, 32 bits wide
  Adder #(.width(32)) adder_1 (
    .a(multiplexer_1_out), .b(multiplexer_2_out), .out(adder_1_out), .cin(CarryIn), .cout(CarryOut));
  Multiplexer #(.select(2), .width(32)) multiplexer_3 (
    .in0(and_1_out), .in1(or_1_out), .in2(adder_1_out), .in3({{31{1'b0}}, adder_1_out[31]}), .out(Result),
    .sel(Operation));  // open: en
  or or_2 (Zero, Result[0], Result[1], Result[2], Result[3], Result[4], Result[5], Result[6], Result[7], Result[8], Result[9], Result[10], Result[11], Result[12], Result[13], Result[14], Result[15], Result[16], Result[17], Result[18], Result[19], Result[20], Result[21], Result[22], Result[23], Result[24], Result[25], Result[26], Result[27], Result[28], Result[29], Result[30], Result[31]);
endmodule
