// Logisim project ledDisplay (1).circ as structural Verilog: 11 circuits, main circuit main
module main (
  output [31:0] out_1
);

  wire alu_to_do_1_zero, Beq_out, Bne_out, clock_1_out, cpu_control_to_do_1_ainvert,
       cpu_control_to_do_1_alusrc, cpu_control_to_do_1_bne, cpu_control_to_do_1_bnegate,
       cpu_control_to_do_1_branch, cpu_control_to_do_1_byte, cpu_control_to_do_1_half,
       cpu_control_to_do_1_jal, cpu_control_to_do_1_jr, cpu_control_to_do_1_jump, cpu_control_to_do_1_lui,
       cpu_control_to_do_1_memread, cpu_control_to_do_1_memtoreg, cpu_control_to_do_1_memwrite,
       cpu_control_to_do_1_regdst, cpu_control_to_do_1_regshift, cpu_control_to_do_1_regwrite,
       cpu_control_to_do_1_shift, cpu_control_to_do_1_shift_direction, cpu_control_to_do_1_shift_value,
       cpu_control_to_do_1_word, cpu_control_to_do_1_zeroextend, Jump_out, not_1_out, or_1_out;
  wire [1:0] cpu_control_to_do_1_operation;
  wire [4:0] multiplexer_1_out, multiplexer_2_out, multiplexer_4_out;
  wire [15:0] PC_q_2;
  wire [27:0] shift_left_2_expand_to_do_1_output;
  wire [31:0] adder_1_out, adder_2_out, alu_to_do_1_result, main_memory_1__000, main_memory_1__001,
       main_memory_1__010, main_memory_1__011, main_memory_1__100, main_memory_1__101, main_memory_1__110,
       main_memory_1__111, main_memory_1_data, multiplexer_3_out, multiplexer_5_out, multiplexer_6_out,
       multiplexer_7_out, multiplexer_8_out, multiplexer_9_out, multiplexer_10_out, PC_q,
       register_file_to_do_1_readreg_1_value, register_file_to_do_1_readreg_2_value,
       shift_left_2_to_do_1_output, sign_extend_to_do_1_output, zero_extend_to_do_1_output;

  Register #(.width(32), .trigger("falling")) PC (
    .D(multiplexer_9_out), .Q({PC_q[31:18], PC_q_2, PC_q[1:0]}), .clk(clock_1_out));  // open: en, clr
  Adder #(.width(32)) adder_1 (.a({PC_q[31:18], PC_q_2, PC_q[1:0]}), .b(32'h4), .out(adder_1_out));  // open: cin, cout
  ROM #(.addrWidth(16), .dataWidth(32)) rom_1 (.addr(PC_q_2), .data(out_1));  // open: sel
  CPU_Control__TO_DO cpu_control_to_do_1 (
    .Funct(out_1[5:0]), .Opcode(out_1[31:26]), .RegDst(cpu_control_to_do_1_regdst),
    .Jump(cpu_control_to_do_1_jump), .Branch(cpu_control_to_do_1_branch),
    .MemRead(cpu_control_to_do_1_memread), .MemtoReg(cpu_control_to_do_1_memtoreg),
    .MemWrite(cpu_control_to_do_1_memwrite), .ALUSrc(cpu_control_to_do_1_alusrc),
    .RegWrite(cpu_control_to_do_1_regwrite), .bne(cpu_control_to_do_1_bne), .jal(cpu_control_to_do_1_jal),
    .jr(cpu_control_to_do_1_jr), .lui(cpu_control_to_do_1_lui), .Shift(cpu_control_to_do_1_shift),
    .Shift_Direction(cpu_control_to_do_1_shift_direction), .Shift_Value(cpu_control_to_do_1_shift_value),
    .Byte(cpu_control_to_do_1_byte), .Half(cpu_control_to_do_1_half), .Word(cpu_control_to_do_1_word),
    .ZeroExtend(cpu_control_to_do_1_zeroextend), .Ainvert(cpu_control_to_do_1_ainvert),
    .Bnegate(cpu_control_to_do_1_bnegate), .Operation(cpu_control_to_do_1_operation),
    .RegShift(cpu_control_to_do_1_regshift));
  Shift_Left_2_Expand__TO_DO shift_left_2_expand_to_do_1 (
    .Input(out_1[25:0]), .Output(shift_left_2_expand_to_do_1_output));
  Multiplexer #(.width(5)) multiplexer_1 (
    .in0(out_1[20:16]), .in1(out_1[15:11]), .out(multiplexer_1_out), .sel(cpu_control_to_do_1_regdst));  // open: en
  Multiplexer #(.width(5)) multiplexer_2 (
    .in0(multiplexer_1_out), .in1({5{1'b1}}), .out(multiplexer_2_out), .sel(cpu_control_to_do_1_jal));  // open: en
  Multiplexer #(.width(32)) multiplexer_3 (
    .in0(multiplexer_10_out), .in1(adder_1_out), .out(multiplexer_3_out), .sel(cpu_control_to_do_1_jal));  // open: en
  Clock clock_1 (.out(clock_1_out));
  Sign_Extend__TO_DO sign_extend_to_do_1 (.Input(out_1[15:0]), .Output(sign_extend_to_do_1_output));
  Zero_Extend__TO_DO zero_extend_to_do_1 (.\input (out_1[15:0]), .Output(zero_extend_to_do_1_output));
  Multiplexer #(.width(5)) multiplexer_4 (
    .in0(out_1[25:21]), .in1(out_1[20:16]), .out(multiplexer_4_out), .sel(cpu_control_to_do_1_regshift));  // open: en
  Register_File__TO_DO register_file_to_do_1 (
    .Read_Register_1(multiplexer_4_out), .Read_Register_2(out_1[20:16]), .Write_Register(multiplexer_2_out),
    .Write_Data(multiplexer_3_out), .Write_Enable(cpu_control_to_do_1_regwrite), .Clock(clock_1_out),
    .ReadReg_1_Value(register_file_to_do_1_readreg_1_value),
    .ReadReg_2_Value(register_file_to_do_1_readreg_2_value));
  Multiplexer #(.width(32)) multiplexer_5 (
    .in0(sign_extend_to_do_1_output), .in1(zero_extend_to_do_1_output), .out(multiplexer_5_out),
    .sel(cpu_control_to_do_1_zeroextend));  // open: en
  Shift_Left_2__TO_DO shift_left_2_to_do_1 (.Input(multiplexer_5_out), .Output(shift_left_2_to_do_1_output));
  Adder #(.width(32)) adder_2 (.a(adder_1_out), .b(shift_left_2_to_do_1_output), .out(adder_2_out));  // open: cin, cout
  Multiplexer #(.width(32)) multiplexer_6 (
    .in0(register_file_to_do_1_readreg_2_value), .in1(multiplexer_5_out), .out(multiplexer_6_out),
    .sel(cpu_control_to_do_1_alusrc));  // open: en
  or Jump (Jump_out, cpu_control_to_do_1_jal, cpu_control_to_do_1_jump);
  Multiplexer #(.width(32)) multiplexer_7 (
    .in0(adder_1_out), .in1(adder_2_out), .out(multiplexer_7_out), .sel(or_1_out));  // open: en
  Multiplexer #(.width(32)) multiplexer_8 (
    .in0(multiplexer_7_out), .in1({adder_1_out[31:28], shift_left_2_expand_to_do_1_output}),
    .out(multiplexer_8_out), .sel(Jump_out));  // open: en
  Multiplexer #(.width(32)) multiplexer_9 (
    .in0(multiplexer_8_out), .in1(register_file_to_do_1_readreg_1_value), .out(multiplexer_9_out),
    .sel(cpu_control_to_do_1_jr));  // open: en
  and Beq (Beq_out, cpu_control_to_do_1_branch, alu_to_do_1_zero);
  not not_1 (not_1_out, alu_to_do_1_zero);
  ALU__TO_DO alu_to_do_1 (
    .a(register_file_to_do_1_readreg_1_value), .b(multiplexer_6_out),
    .Shift_Value(cpu_control_to_do_1_shift_value), .lui(cpu_control_to_do_1_lui),
    .Ainvert(cpu_control_to_do_1_ainvert), .Binvert(cpu_control_to_do_1_bnegate),
    .Operation(cpu_control_to_do_1_operation), .Shift_Direction(cpu_control_to_do_1_shift_direction),
    .Shift(cpu_control_to_do_1_shift), .Zero(alu_to_do_1_zero), .Result(alu_to_do_1_result));  // open: CarryOut
  DotMatrix #(.matrixcols(8), .matrixrows(8), .dotshape("circle")) dotmatrix_1 (
    .col0(main_memory_1__111[31:24]), .col1(main_memory_1__111[23:16]), .col2(main_memory_1__111[15:8]),
    .col3(main_memory_1__111[7:0]), .col4(main_memory_1__110[31:24]), .col5(main_memory_1__110[23:16]),
    .col6(main_memory_1__110[15:8]), .col7(main_memory_1__110[7:0]));
  or or_1 (or_1_out, Beq_out, Bne_out);
  and Bne (Bne_out, cpu_control_to_do_1_bne, not_1_out);
  DotMatrix #(.matrixcols(8), .matrixrows(8), .dotshape("circle")) dotmatrix_2 (
    .col0(main_memory_1__101[31:24]), .col1(main_memory_1__101[23:16]), .col2(main_memory_1__101[15:8]),
    .col3(main_memory_1__101[7:0]), .col4(main_memory_1__100[31:24]), .col5(main_memory_1__100[23:16]),
    .col6(main_memory_1__100[15:8]), .col7(main_memory_1__100[7:0]));
  DotMatrix #(.matrixcols(8), .matrixrows(8), .dotshape("circle")) dotmatrix_3 (
    .col0(main_memory_1__011[31:24]), .col1(main_memory_1__011[23:16]), .col2(main_memory_1__011[15:8]),
    .col3(main_memory_1__011[7:0]), .col4(main_memory_1__010[31:24]), .col5(main_memory_1__010[23:16]),
    .col6(main_memory_1__010[15:8]), .col7(main_memory_1__010[7:0]));
  DotMatrix #(.matrixcols(8), .matrixrows(8), .dotshape("circle")) dotmatrix_4 (
    .col0(main_memory_1__001[31:24]), .col1(main_memory_1__001[23:16]), .col2(main_memory_1__001[15:8]),
    .col3(main_memory_1__001[7:0]), .col4(main_memory_1__000[31:24]), .col5(main_memory_1__000[23:16]),
    .col6(main_memory_1__000[15:8]), .col7(main_memory_1__000[7:0]));
  Main_Memory main_memory_1 (
    .Address(alu_to_do_1_result), .DataToWrite(register_file_to_do_1_readreg_2_value),
    .\byte (cpu_control_to_do_1_byte), .half(cpu_control_to_do_1_half), .word(cpu_control_to_do_1_word),
    .MemWrite(cpu_control_to_do_1_memwrite), ._111(main_memory_1__111), ._110(main_memory_1__110),
    ._101(main_memory_1__101), ._100(main_memory_1__100), ._011(main_memory_1__011),
    ._010(main_memory_1__010), ._001(main_memory_1__001), ._000(main_memory_1__000), .clock(clock_1_out),
    .MemRead(cpu_control_to_do_1_memread), .Data(main_memory_1_data));
  Multiplexer #(.width(32)) multiplexer_10 (
    .in0(alu_to_do_1_result), .in1(main_memory_1_data), .out(multiplexer_10_out),
    .sel(cpu_control_to_do_1_memtoreg));  // open: en

  // Notes on the sheet:
  //   contents of rom_1 (hex, n*v repeats v):
  //   3c1d7fff 37bdeffc 3c111001 36310120 92320000 12400004 122020 c10000b 22310001 8100004 810000a
  //   23bdfff4 afb10008 afb00004 afbf0000 20100020 1604000d 2020 c100040 2020 c100040 2020 c100040 2020
  //   c100040 2020 c100040 2020 c100040 810003b 2010003a 90802a 12000004 2090ffd0 3c111001 363100d0
  //   8100027 2090ffbf 3c111001 1080c0 2308820 8e300000 102600 42602 c100040 102400 42602 c100040 102200
  //   42602 c100040 102602 c100040 8e300004 102600 42602 c100040 2020 c100040 8fb10008 8fb00004 8fbf0000
  //   23bd000c 3e00008 44020 3c09ffff 35298000 200a0007 1140000a a5880 12b5820 8d6c0000 8d6dfffc c6200
  //   d6e02 18d6025 ad6c0000 214affff 8100044 8d2a0000 a5200 1485025 ad2a0000 3e00008
endmodule

module _8_Word_Direct_Output (
  input  MemWrite,
  input  [31:0] Address,
  input  [31:0] DataIn,
  input  Clock,
  output [31:0] _000,
  output [31:0] _001,
  output [31:0] _010,
  output [31:0] _011,
  output [31:0] _100,
  output [31:0] _101,
  output [31:0] _110,
  output [31:0] _111,
  output [31:0] DataOut
);

  wire and_1_out, and_2_out, and_3_out, and_4_out, and_5_out, and_6_out, and_7_out, and_8_out,
       decoder_1_out0, decoder_1_out1, decoder_1_out2, decoder_1_out3, decoder_1_out4, decoder_1_out5,
       decoder_1_out6, decoder_1_out7;

  Decoder #(.select(3)) decoder_1 (
    .out0(decoder_1_out0), .out1(decoder_1_out1), .out2(decoder_1_out2), .out3(decoder_1_out3),
    .out4(decoder_1_out4), .out5(decoder_1_out5), .out6(decoder_1_out6), .out7(decoder_1_out7),
    .sel(Address[4:2]));  // open: en
  and and_1 (and_1_out, MemWrite, decoder_1_out0);
  and and_2 (and_2_out, MemWrite, decoder_1_out1);
  and and_3 (and_3_out, MemWrite, decoder_1_out2);
  and and_4 (and_4_out, MemWrite, decoder_1_out3);
  and and_5 (and_5_out, MemWrite, decoder_1_out4);
  and and_6 (and_6_out, MemWrite, decoder_1_out5);
  and and_7 (and_7_out, MemWrite, decoder_1_out6);
  and and_8 (and_8_out, MemWrite, decoder_1_out7);
  Register #(.width(32), .trigger("falling")) register_1 (
    .D(DataIn), .en(and_1_out), .Q(_000), .clk(Clock));  // open: clr
  Register #(.width(32), .trigger("falling")) register_2 (
    .D(DataIn), .en(and_2_out), .Q(_001), .clk(Clock));  // open: clr
  Register #(.width(32), .trigger("falling")) register_3 (
    .D(DataIn), .en(and_3_out), .Q(_010), .clk(Clock));  // open: clr
  Register #(.width(32), .trigger("falling")) register_4 (
    .D(DataIn), .en(and_4_out), .Q(_011), .clk(Clock));  // open: clr
  Register #(.width(32), .trigger("falling")) register_5 (
    .D(DataIn), .en(and_5_out), .Q(_100), .clk(Clock));  // open: clr
  Register #(.width(32), .trigger("falling")) register_6 (
    .D(DataIn), .en(and_6_out), .Q(_101), .clk(Clock));  // open: clr
  Register #(.width(32), .trigger("falling")) register_7 (
    .D(DataIn), .en(and_7_out), .Q(_110), .clk(Clock));  // open: clr
  Register #(.width(32), .trigger("falling")) register_8 (
    .D(DataIn), .en(and_8_out), .Q(_111), .clk(Clock));  // open: clr
  Multiplexer #(.select(3), .width(32)) multiplexer_1 (
    .in0(_000), .in1(_001), .in2(_010), .in3(_011), .in4(_100), .in5(_101), .in6(_110), .in7(_111),
    .out(DataOut), .sel(Address[4:2]));  // open: en
endmodule

module Main_Memory (
  input  MemWrite,
  input  [31:0] Address,
  input  [31:0] DataToWrite,
  input  \byte ,
  input  half,
  input  word,
  input  clock,
  input  MemRead,
  output [31:0] _111,
  output [31:0] _110,
  output [31:0] _101,
  output [31:0] _100,
  output [31:0] _011,
  output [31:0] _010,
  output [31:0] _001,
  output [31:0] _000,
  output [31:0] Data
);

  wire address_comparator_1_active, address_comparator_2_active, address_comparator_3_active, and_3_out,
       and_4_out, and_5_out, and_6_out, and_7_out, not_1_out, not_2_out, not_3_out, not_4_out;
  wire [1:0] address_comparator_1_output_address_2, and_2_out;
  wire [7:0] multiplexer_5_out;
  wire [15:0] multiplexer_4_out;
  wire [31:0] address_comparator_2_output_address, address_comparator_3_output_address,
       controlled_buffer_1_out, multiplexer_1_out, multiplexer_2_out, multiplexer_3_out,
       n8_word_direct_output_1_dataout, ram_1_data, ram_2_data;
  wire [31:2] address_comparator_1_output_address;

  Address_Comparator address_comparator_1 (
    .Input_Address(Address), .Starting_Address(32'h10010000), .Memory_Size(32'h4000000), .isStack(1'b0),
    .Active(address_comparator_1_active),
    .Output_Address({address_comparator_1_output_address, address_comparator_1_output_address_2}));
  Address_Comparator address_comparator_2 (
    .Input_Address(Address), .Starting_Address(32'h7fffeffc), .Memory_Size(32'h4000000), .isStack(1'b1),
    .Active(address_comparator_2_active), .Output_Address(address_comparator_2_output_address));
  Address_Comparator address_comparator_3 (
    .Input_Address(Address), .Starting_Address(32'hffff8000), .Memory_Size(32'h20), .isStack(1'b0),
    .Active(address_comparator_3_active), .Output_Address(address_comparator_3_output_address));
  not not_1 (not_1_out, \byte );
  not not_2 (not_2_out, half);
  not not_3 (not_3_out, word);
  and and_1 (and_2_out[1], \byte , not_2_out, not_3_out);
  and and_2 (and_2_out[0], not_1_out, half, not_3_out);
  Multiplexer #(.select(2), .width(32)) multiplexer_1 (
    .in0({controlled_buffer_1_out[31:8], DataToWrite[7:0]}),
    .in1({controlled_buffer_1_out[31:16], DataToWrite[7:0], controlled_buffer_1_out[7:0]}),
    .in2({controlled_buffer_1_out[31:24], DataToWrite[7:0], controlled_buffer_1_out[15:0]}),
    .in3({DataToWrite[7:0], controlled_buffer_1_out[23:0]}), .out(multiplexer_1_out),
    .sel(address_comparator_1_output_address_2));  // open: en
  Multiplexer #(.width(32)) multiplexer_2 (
    .in0({controlled_buffer_1_out[31:16], DataToWrite[15:0]}),
    .in1({DataToWrite[15:0], controlled_buffer_1_out[15:0]}), .out(multiplexer_2_out),
    .sel(address_comparator_1_output_address_2[1]));  // open: en
  Multiplexer #(.select(2), .width(32)) multiplexer_3 (
    .in0(DataToWrite), .in1(multiplexer_2_out), .in2(multiplexer_1_out), .out(multiplexer_3_out),
    .sel(and_2_out));  // open: in3, en
  and and_3 (and_3_out, MemWrite, and_6_out);
  and and_4 (and_4_out, MemWrite, address_comparator_2_active);
  and and_5 (and_5_out, address_comparator_3_active, MemWrite);
  _8_Word_Direct_Output u_8_word_direct_output_1 (
    .Address(address_comparator_3_output_address), .DataIn(multiplexer_3_out), .MemWrite(and_5_out),
    .Clock(clock), ._000(_000), ._001(_001), ._010(_010), ._011(_011), ._100(_100), ._101(_101), ._110(_110),
    ._111(_111), .DataOut(n8_word_direct_output_1_dataout));
  assign controlled_buffer_1_out = address_comparator_3_active ? n8_word_direct_output_1_dataout : 32'bz;  // Controlled_Buffer controlled_buffer_1
  not not_4 (not_4_out, address_comparator_3_active);
  RAM #(.addrWidth(24), .dataWidth(32), .bus("separate")) ram_1 (
    .addr(address_comparator_1_output_address[25:2]), .din(multiplexer_3_out), .data(ram_1_data),
    .str(and_3_out), .clk(clock));  // open: sel, ld, clr
  RAM #(.addrWidth(24), .dataWidth(32), .bus("separate")) ram_2 (
    .addr(address_comparator_2_output_address[25:2]), .din(multiplexer_3_out), .data(ram_2_data),
    .str(and_4_out), .clk(clock));  // open: sel, ld, clr
  assign controlled_buffer_1_out = and_6_out ? ram_1_data : 32'bz;  // Controlled_Buffer controlled_buffer_2
  and and_6 (and_6_out, not_4_out, address_comparator_1_active);
  assign controlled_buffer_1_out = and_7_out ? ram_2_data : 32'bz;  // Controlled_Buffer controlled_buffer_3
  and and_7 (and_7_out, not_4_out, address_comparator_2_active);
  Multiplexer #(.width(16)) multiplexer_4 (
    .in0(controlled_buffer_1_out[15:0]), .in1(controlled_buffer_1_out[31:16]), .out(multiplexer_4_out),
    .sel(address_comparator_1_output_address_2[1]));  // open: en
  Multiplexer #(.select(2), .width(8)) multiplexer_5 (
    .in0(controlled_buffer_1_out[7:0]), .in1(controlled_buffer_1_out[15:8]),
    .in2(controlled_buffer_1_out[23:16]), .in3(controlled_buffer_1_out[31:24]), .out(multiplexer_5_out),
    .sel(address_comparator_1_output_address_2));  // open: en
  Multiplexer #(.select(2), .width(32)) multiplexer_6 (
    .in0(controlled_buffer_1_out), .in1({{16{1'b0}}, multiplexer_4_out}),
    .in2({{24{1'b0}}, multiplexer_5_out}), .in3({32{1'b0}}), .out(Data), .sel(and_2_out), .en(MemRead));
endmodule

module Address_Comparator (
  input  [31:0] Input_Address,
  input  [31:0] Starting_Address,
  input  [31:0] Memory_Size,
  input  isStack,
  output Active,
  output [31:0] Output_Address
);

  wire and_1_out, and_2_out, comparator_1_eq, comparator_1_gt, comparator_2_lt, comparator_3_eq,
       comparator_3_lt, comparator_4_gt, or_1_out, or_2_out;
  wire [31:0] adder_1_out, subtractor_1_out, subtractor_2_out, subtractor_3_out;

  Comparator #(.width(32), .mode("unsigned")) comparator_1 (
    .a(Input_Address), .b(Starting_Address), .gt(comparator_1_gt), .eq(comparator_1_eq));  // open: lt
  Comparator #(.width(32), .mode("unsigned")) comparator_2 (
    .a(Input_Address), .b(adder_1_out), .lt(comparator_2_lt));  // open: gt, eq
  Adder #(.width(32)) adder_1 (.a(Starting_Address), .b(Memory_Size), .out(adder_1_out));  // open: cin, cout
  Subtractor #(.width(32)) subtractor_1 (
    .a(Input_Address), .b(Starting_Address), .out(subtractor_1_out));  // open: bin, bout
  Comparator #(.width(32), .mode("unsigned")) comparator_3 (
    .a(Input_Address), .b(Starting_Address), .eq(comparator_3_eq), .lt(comparator_3_lt));  // open: gt
  Comparator #(.width(32), .mode("unsigned")) comparator_4 (
    .a(Input_Address), .b(subtractor_2_out), .gt(comparator_4_gt));  // open: eq, lt
  Subtractor #(.width(32)) subtractor_2 (
    .a(Starting_Address), .b(Memory_Size), .out(subtractor_2_out));  // open: bin, bout
  Subtractor #(.width(32)) subtractor_3 (
    .a(Starting_Address), .b(Input_Address), .out(subtractor_3_out));  // open: bin, bout
  or or_1 (or_1_out, comparator_1_gt, comparator_1_eq);
  and and_1 (and_1_out, or_1_out, comparator_2_lt);
  or or_2 (or_2_out, comparator_3_eq, comparator_3_lt);
  and and_2 (and_2_out, or_2_out, comparator_4_gt);
  Multiplexer multiplexer_1 (.in0(and_1_out), .in1(and_2_out), .out(Active), .sel(isStack));  // open: en
  Multiplexer #(.width(32)) multiplexer_2 (
    .in0(subtractor_1_out), .in1(subtractor_3_out), .out(Output_Address), .sel(isStack));  // open: en
endmodule

module ALU__TO_DO (
  input  Ainvert,
  input  Binvert,
  input  [1:0] Operation,
  input  Shift_Direction,
  input  Shift,
  input  Shift_Value,
  input  lui,
  input  [31:0] a,
  input  [31:0] b,
  output Zero,
  output [31:0] Result,
  output CarryOut
);

  wire or_2_out;
  wire [4:0] multiplexer_3_out, multiplexer_7_out;
  wire [31:0] adder_1_out, adder_2_out, adder_3_out, and_1_out, multiplexer_1_out, multiplexer_2_out,
       multiplexer_4_out, multiplexer_5_out, multiplexer_6_out, multiplexer_8_out, multiplexer_9_out,
       not_1_out, not_2_out, or_1_out, shifter_1_out, shifter_2_out;

  assign not_1_out = ~a;  // NOT_Gate not_1, 32 bits wide
  assign not_2_out = ~b;  // NOT_Gate not_2, 32 bits wide
  Adder #(.width(32)) adder_1 (.a(not_1_out), .b(32'h1), .out(adder_1_out));  // open: cin, cout
  Adder #(.width(32)) adder_2 (.a(not_2_out), .b(32'h1), .out(adder_2_out));  // open: cin, cout
  Multiplexer #(.select(2), .width(32)) multiplexer_1 (
    .in0(not_1_out), .in1(not_1_out), .in2(adder_1_out), .in3(not_1_out), .out(multiplexer_1_out),
    .sel(Operation));  // open: en
  Multiplexer #(.select(2), .width(32)) multiplexer_2 (
    .in0(not_2_out), .in1(not_2_out), .in2(adder_2_out), .in3(not_2_out), .out(multiplexer_2_out),
    .sel(Operation));  // open: en
  Multiplexer #(.width(5)) multiplexer_3 (
    .in0(b[10:6]), .in1(a[4:0]), .out(multiplexer_3_out), .sel(Shift_Value));  // open: en
  Multiplexer #(.width(32)) multiplexer_4 (
    .in0(a), .in1(multiplexer_1_out), .out(multiplexer_4_out), .sel(Ainvert));  // open: en
  Multiplexer #(.width(32)) multiplexer_5 (
    .in0(b), .in1(multiplexer_2_out), .out(multiplexer_5_out), .sel(Binvert));  // open: en
  Multiplexer #(.width(32)) multiplexer_6 (
    .in0(multiplexer_4_out), .in1(multiplexer_5_out), .out(multiplexer_6_out), .sel(Shift_Value));  // open: en
  Multiplexer #(.width(5)) multiplexer_7 (
    .in0(multiplexer_3_out), .in1(5'b10000), .out(multiplexer_7_out), .sel(lui));  // open: en
  assign and_1_out = multiplexer_4_out & multiplexer_5_out;  // AND_Gate and_1, 32 bits wide
  assign or_1_out = multiplexer_4_out | multiplexer_5_out;  // OR_Gate or_1, 32 bits wide
  Adder #(.width(32)) adder_3 (
    .a(multiplexer_4_out), .b(multiplexer_5_out), .out(adder_3_out), .cout(CarryOut));  // open: cin
  Shifter #(.width(32)) shifter_1 (.in(multiplexer_6_out), .\dist (multiplexer_7_out), .out(shifter_1_out));
  Shifter #(.width(32), .shift("lr")) shifter_2 (
    .in(multiplexer_6_out), .\dist (multiplexer_3_out), .out(shifter_2_out));
  Multiplexer #(.select(2), .width(32)) multiplexer_8 (
    .in0(and_1_out), .in1(or_1_out), .in2(adder_3_out), .in3({{31{1'b0}}, adder_3_out[31]}),
    .out(multiplexer_8_out), .sel(Operation));  // open: en
  Multiplexer #(.width(32)) multiplexer_9 (
    .in0(shifter_1_out), .in1(shifter_2_out), .out(multiplexer_9_out), .sel(Shift_Direction));  // open: en
  Multiplexer #(.width(32)) multiplexer_10 (
    .in0(multiplexer_8_out), .in1(multiplexer_9_out), .out(Result), .sel(Shift));  // open: en
  not not_3 (Zero, or_2_out);
  or or_2 (or_2_out, multiplexer_8_out[0], multiplexer_8_out[1], multiplexer_8_out[2], multiplexer_8_out[3], multiplexer_8_out[4], multiplexer_8_out[5], multiplexer_8_out[6], multiplexer_8_out[7], multiplexer_8_out[8], multiplexer_8_out[9], multiplexer_8_out[10], multiplexer_8_out[11], multiplexer_8_out[12], multiplexer_8_out[13], multiplexer_8_out[14], multiplexer_8_out[15], multiplexer_8_out[16], multiplexer_8_out[17], multiplexer_8_out[18], multiplexer_8_out[19], multiplexer_8_out[20], multiplexer_8_out[21], multiplexer_8_out[22], multiplexer_8_out[23], multiplexer_8_out[24], multiplexer_8_out[25], multiplexer_8_out[26], multiplexer_8_out[27], multiplexer_8_out[28], multiplexer_8_out[29], multiplexer_8_out[30], multiplexer_8_out[31]);
endmodule

module Register_File__TO_DO (
  input  Write_Enable,
  input  [4:0] Read_Register_1,
  input  [4:0] Read_Register_2,
  input  [4:0] Write_Register,
  input  [31:0] Write_Data,
  input  Clock,
  output [31:0] ReadReg_1_Value,
  output [31:0] ReadReg_2_Value
);

  wire and_1_out, and_2_out, and_3_out, and_4_out, and_5_out, and_6_out, and_7_out, and_8_out, and_9_out,
       and_10_out, and_11_out, and_12_out, and_13_out, and_14_out, and_15_out, and_16_out, and_17_out,
       and_18_out, and_19_out, and_20_out, and_21_out, and_22_out, and_23_out, and_24_out, and_25_out,
       and_26_out, and_27_out, and_28_out, and_29_out, and_30_out, and_31_out, and_32_out, decoder_1_out0,
       decoder_1_out1, decoder_1_out2, decoder_1_out3, decoder_1_out4, decoder_1_out5, decoder_1_out6,
       decoder_1_out7, decoder_1_out8, decoder_1_out9, decoder_1_out10, decoder_1_out11, decoder_1_out12,
       decoder_1_out13, decoder_1_out14, decoder_1_out15, decoder_1_out16, decoder_1_out17, decoder_1_out18,
       decoder_1_out19, decoder_1_out20, decoder_1_out21, decoder_1_out22, decoder_1_out23, decoder_1_out24,
       decoder_1_out25, decoder_1_out26, decoder_1_out27, decoder_1_out28, decoder_1_out29, decoder_1_out30,
       decoder_1_out31;
  wire [31:0] Register1_q, Register2_q, Register3_q, Register4_q, Register5_q, Register6_q, Register7_q,
       Register8_q, Register9_q, Register10_q, Register11_q, Register12_q, Register13_q, Register14_q,
       Register15_q, Register16_q, Register17_q, Register18_q, Register19_q, Register20_q, Register21_q,
       Register22_q, Register23_q, Register24_q, Register25_q, Register26_q, Register27_q, Register28_q,
       Register29_q, Register30_q, Register31_q, Register32_q;

  Decoder #(.select(5)) decoder_1 (
    .out0(decoder_1_out0), .out1(decoder_1_out1), .out2(decoder_1_out2), .out3(decoder_1_out3),
    .out4(decoder_1_out4), .out5(decoder_1_out5), .out6(decoder_1_out6), .out7(decoder_1_out7),
    .out8(decoder_1_out8), .out9(decoder_1_out9), .out10(decoder_1_out10), .out11(decoder_1_out11),
    .out12(decoder_1_out12), .out13(decoder_1_out13), .out14(decoder_1_out14), .out15(decoder_1_out15),
    .out16(decoder_1_out16), .out17(decoder_1_out17), .out18(decoder_1_out18), .out19(decoder_1_out19),
    .out20(decoder_1_out20), .out21(decoder_1_out21), .out22(decoder_1_out22), .out23(decoder_1_out23),
    .out24(decoder_1_out24), .out25(decoder_1_out25), .out26(decoder_1_out26), .out27(decoder_1_out27),
    .out28(decoder_1_out28), .out29(decoder_1_out29), .out30(decoder_1_out30), .out31(decoder_1_out31),
    .sel(Write_Register));  // open: en
  and and_1 (and_1_out, Write_Enable, decoder_1_out0);
  and and_2 (and_2_out, Write_Enable, decoder_1_out1);
  and and_3 (and_3_out, Write_Enable, decoder_1_out2);
  and and_4 (and_4_out, Write_Enable, decoder_1_out3);
  and and_5 (and_5_out, Write_Enable, decoder_1_out4);
  and and_6 (and_6_out, Write_Enable, decoder_1_out5);
  and and_7 (and_7_out, Write_Enable, decoder_1_out6);
  and and_8 (and_8_out, Write_Enable, decoder_1_out7);
  and and_9 (and_9_out, Write_Enable, decoder_1_out8);
  and and_10 (and_10_out, Write_Enable, decoder_1_out9);
  and and_11 (and_11_out, Write_Enable, decoder_1_out10);
  and and_12 (and_12_out, Write_Enable, decoder_1_out11);
  and and_13 (and_13_out, Write_Enable, decoder_1_out12);
  and and_14 (and_14_out, Write_Enable, decoder_1_out13);
  and and_15 (and_15_out, Write_Enable, decoder_1_out14);
  and and_16 (and_16_out, Write_Enable, decoder_1_out15);
  and and_17 (and_17_out, Write_Enable, decoder_1_out16);
  and and_18 (and_18_out, Write_Enable, decoder_1_out17);
  and and_19 (and_19_out, Write_Enable, decoder_1_out18);
  and and_20 (and_20_out, Write_Enable, decoder_1_out19);
  and and_21 (and_21_out, Write_Enable, decoder_1_out20);
  and and_22 (and_22_out, Write_Enable, decoder_1_out21);
  and and_23 (and_23_out, Write_Enable, decoder_1_out22);
  and and_24 (and_24_out, Write_Enable, decoder_1_out23);
  and and_25 (and_25_out, Write_Enable, decoder_1_out24);
  and and_26 (and_26_out, Write_Enable, decoder_1_out25);
  and and_27 (and_27_out, Write_Enable, decoder_1_out26);
  and and_28 (and_28_out, Write_Enable, decoder_1_out27);
  and and_29 (and_29_out, Write_Enable, decoder_1_out28);
  and and_30 (and_30_out, Write_Enable, decoder_1_out29);
  and and_31 (and_31_out, Write_Enable, decoder_1_out30);
  and and_32 (and_32_out, Write_Enable, decoder_1_out31);
  Register #(.width(32)) Register1 (.D(Write_Data), .en(and_1_out), .Q(Register1_q), .clk(Clock));  // open: clr
  Register #(.width(32)) Register2 (.D(Write_Data), .en(and_2_out), .Q(Register2_q), .clk(Clock));  // open: clr
  Register #(.width(32)) Register3 (.D(Write_Data), .en(and_3_out), .Q(Register3_q), .clk(Clock));  // open: clr
  Register #(.width(32)) Register4 (.D(Write_Data), .en(and_4_out), .Q(Register4_q), .clk(Clock));  // open: clr
  Register #(.width(32)) Register5 (.D(Write_Data), .en(and_5_out), .Q(Register5_q), .clk(Clock));  // open: clr
  Register #(.width(32)) Register6 (.D(Write_Data), .en(and_6_out), .Q(Register6_q), .clk(Clock));  // open: clr
  Register #(.width(32)) Register7 (.D(Write_Data), .en(and_7_out), .Q(Register7_q), .clk(Clock));  // open: clr
  Register #(.width(32)) Register8 (.D(Write_Data), .en(and_8_out), .Q(Register8_q), .clk(Clock));  // open: clr
  Register #(.width(32)) Register9 (.D(Write_Data), .en(and_9_out), .Q(Register9_q), .clk(Clock));  // open: clr
  Register #(.width(32)) Register10 (.D(Write_Data), .en(and_10_out), .Q(Register10_q), .clk(Clock));  // open: clr
  Register #(.width(32)) Register11 (.D(Write_Data), .en(and_11_out), .Q(Register11_q), .clk(Clock));  // open: clr
  Register #(.width(32)) Register12 (.D(Write_Data), .en(and_12_out), .Q(Register12_q), .clk(Clock));  // open: clr
  Register #(.width(32)) Register13 (.D(Write_Data), .en(and_13_out), .Q(Register13_q), .clk(Clock));  // open: clr
  Register #(.width(32)) Register14 (.D(Write_Data), .en(and_14_out), .Q(Register14_q), .clk(Clock));  // open: clr
  Register #(.width(32)) Register15 (.D(Write_Data), .en(and_15_out), .Q(Register15_q), .clk(Clock));  // open: clr
  Register #(.width(32)) Register16 (.D(Write_Data), .en(and_16_out), .Q(Register16_q), .clk(Clock));  // open: clr
  Register #(.width(32)) Register17 (.D(Write_Data), .en(and_17_out), .Q(Register17_q), .clk(Clock));  // open: clr
  Register #(.width(32)) Register18 (.D(Write_Data), .en(and_18_out), .Q(Register18_q), .clk(Clock));  // open: clr
  Register #(.width(32)) Register19 (.D(Write_Data), .en(and_19_out), .Q(Register19_q), .clk(Clock));  // open: clr
  Register #(.width(32)) Register20 (.D(Write_Data), .en(and_20_out), .Q(Register20_q), .clk(Clock));  // open: clr
  Register #(.width(32)) Register21 (.D(Write_Data), .en(and_21_out), .Q(Register21_q), .clk(Clock));  // open: clr
  Register #(.width(32)) Register22 (.D(Write_Data), .en(and_22_out), .Q(Register22_q), .clk(Clock));  // open: clr
  Register #(.width(32)) Register23 (.D(Write_Data), .en(and_23_out), .Q(Register23_q), .clk(Clock));  // open: clr
  Register #(.width(32)) Register24 (.D(Write_Data), .en(and_24_out), .Q(Register24_q), .clk(Clock));  // open: clr
  Register #(.width(32)) Register25 (.D(Write_Data), .en(and_25_out), .Q(Register25_q), .clk(Clock));  // open: clr
  Register #(.width(32)) Register26 (.D(Write_Data), .en(and_26_out), .Q(Register26_q), .clk(Clock));  // open: clr
  Register #(.width(32)) Register27 (.D(Write_Data), .en(and_27_out), .Q(Register27_q), .clk(Clock));  // open: clr
  Register #(.width(32)) Register28 (.D(Write_Data), .en(and_28_out), .Q(Register28_q), .clk(Clock));  // open: clr
  Register #(.width(32)) Register29 (.D(Write_Data), .en(and_29_out), .Q(Register29_q), .clk(Clock));  // open: clr
  Register #(.width(32)) Register30 (.D(Write_Data), .en(and_30_out), .Q(Register30_q), .clk(Clock));  // open: clr
  Register #(.width(32)) Register31 (.D(Write_Data), .en(and_31_out), .Q(Register31_q), .clk(Clock));  // open: clr
  Register #(.width(32)) Register32 (.D(Write_Data), .en(and_32_out), .Q(Register32_q), .clk(Clock));  // open: clr
  Multiplexer #(.select(5), .width(32)) multiplexer_1 (
    .in0(Register1_q), .in1(Register2_q), .in2(Register3_q), .in3(Register4_q), .in4(Register5_q),
    .in5(Register6_q), .in6(Register7_q), .in7(Register8_q), .in8(Register9_q), .in9(Register10_q),
    .in10(Register11_q), .in11(Register12_q), .in12(Register13_q), .in13(Register14_q), .in14(Register15_q),
    .in15(Register16_q), .in16(Register17_q), .in17(Register18_q), .in18(Register19_q), .in19(Register20_q),
    .in20(Register21_q), .in21(Register22_q), .in22(Register23_q), .in23(Register24_q), .in24(Register25_q),
    .in25(Register26_q), .in26(Register27_q), .in27(Register28_q), .in28(Register29_q), .in29(Register30_q),
    .in30(Register31_q), .in31(Register32_q), .out(ReadReg_1_Value), .sel(Read_Register_1));  // open: en
  Multiplexer #(.select(5), .width(32)) multiplexer_2 (
    .in0(Register1_q), .in1(Register2_q), .in2(Register3_q), .in3(Register4_q), .in4(Register5_q),
    .in5(Register6_q), .in6(Register7_q), .in7(Register8_q), .in8(Register9_q), .in9(Register10_q),
    .in10(Register11_q), .in11(Register12_q), .in12(Register13_q), .in13(Register14_q), .in14(Register15_q),
    .in15(Register16_q), .in16(Register17_q), .in17(Register18_q), .in18(Register19_q), .in19(Register20_q),
    .in20(Register21_q), .in21(Register22_q), .in22(Register23_q), .in23(Register24_q), .in24(Register25_q),
    .in25(Register26_q), .in26(Register27_q), .in27(Register28_q), .in28(Register29_q), .in29(Register30_q),
    .in30(Register31_q), .in31(Register32_q), .out(ReadReg_2_Value), .sel(Read_Register_2));  // open: en
endmodule

module Sign_Extend__TO_DO (
  input  [15:0] Input,
  output [31:0] Output
);


  assign Output = {{17{Input[15]}}, Input[14:0]};
endmodule

module Shift_Left_2__TO_DO (
  input  [31:0] Input,
  output [31:0] Output
);

  Shifter #(.width(32)) shifter_1 (.in(Input), .\dist (5'b00010), .out(Output));
endmodule

module Shift_Left_2_Expand__TO_DO (
  input  [25:0] Input,
  output [27:0] Output
);

  Shifter #(.width(26)) shifter_1 (.in(Input), .\dist (5'b00010), .out(Output[25:0]));

  assign Output[27:26] = Input[25:24];
endmodule

module Zero_Extend__TO_DO (
  input  [15:0] \input ,
  output [31:0] Output
);


  assign Output = {{16{1'b0}}, \input };
endmodule

module CPU_Control__TO_DO (
  input  [5:0] Funct,
  input  [5:0] Opcode,
  output RegDst,
  output Jump,
  output Branch,
  output MemRead,
  output MemtoReg,
  output MemWrite,
  output ALUSrc,
  output RegWrite,
  output bne,
  output jal,
  output jr,
  output lui,
  output Shift,
  output Shift_Direction,
  output Shift_Value,
  output Byte,
  output Half,
  output Word,
  output ZeroExtend,
  output Ainvert,
  output Bnegate,
  output [1:0] Operation,
  output RegShift
);

  wire Add_out, Addi_out, And_out, andi_out, lbu_out, lhu_out, lw_out, not_1_out, not_2_out, not_3_out,
       not_4_out, not_5_out, not_6_out, not_7_out, not_8_out, not_9_out, not_10_out, not_11_out, not_12_out,
       not_13_out, Or_out, ori_out, sb_out, sh_out, Sll_out, Sllv_out, Slt_out, Slti_out, Srl_out, Srlv_out,
       Sub_out, Subu_out, sw_out, ZeroOp_out;

  not not_1 (not_1_out, Opcode[4]);
  not not_2 (not_2_out, Opcode[5]);
  not not_3 (not_3_out, Opcode[3]);
  not not_4 (not_4_out, Opcode[1]);
  not not_5 (not_5_out, Opcode[2]);
  not not_6 (not_6_out, Funct[5]);
  not not_7 (not_7_out, Funct[4]);
  not not_8 (not_8_out, Opcode[0]);
  not not_9 (not_9_out, Funct[1]);
  not not_10 (not_10_out, Funct[2]);
  not not_11 (not_11_out, Funct[3]);
  not not_12 (not_12_out, Funct[0]);
  nor ZeroOp (ZeroOp_out, Opcode[0], Opcode[1], Opcode[2], Opcode[3], Opcode[4], Opcode[5]);
  and u_RegDst (RegDst, not_3_out, not_2_out);
  and u_Jump (Jump, not_2_out, not_1_out, not_3_out, not_5_out, Opcode[1], not_8_out);
  and u_Branch (Branch, not_2_out, not_1_out, not_3_out, Opcode[2], not_4_out, not_8_out);
  and u_bne (bne, not_2_out, not_1_out, not_3_out, Opcode[2], not_4_out, Opcode[0]);
  and u_jal (jal, not_2_out, not_1_out, not_3_out, not_5_out, Opcode[1], Opcode[0]);
  and u_jr (jr, ZeroOp_out, not_6_out, not_7_out, Funct[3], not_10_out, not_9_out, not_12_out);
  and u_lui (lui, not_2_out, not_1_out, Opcode[3], Opcode[2], Opcode[1], Opcode[0]);
  and Sll (Sll_out, ZeroOp_out, not_6_out, not_7_out, not_11_out, not_10_out, not_9_out, not_12_out);
  and Sllv (Sllv_out, ZeroOp_out, not_6_out, not_7_out, not_11_out, Funct[2], not_9_out, not_12_out);
  and Srl (Srl_out, ZeroOp_out, not_6_out, not_7_out, not_11_out, not_10_out, Funct[1], not_12_out);
  and Srlv (Srlv_out, ZeroOp_out, not_6_out, not_7_out, not_11_out, Funct[2], Funct[1], not_12_out);
  and lbu (lbu_out, Opcode[5], not_1_out, not_3_out, Opcode[2], not_4_out, not_8_out);
  and sb (sb_out, Opcode[5], not_1_out, Opcode[3], not_5_out, not_4_out, not_8_out);
  and lhu (lhu_out, Opcode[5], not_1_out, not_3_out, Opcode[2], not_4_out, Opcode[0]);
  and sh (sh_out, Opcode[5], not_1_out, Opcode[3], not_5_out, not_4_out, Opcode[0]);
  and lw (lw_out, Opcode[5], not_1_out, not_3_out, not_5_out, Opcode[1], Opcode[0]);
  and sw (sw_out, Opcode[5], not_1_out, Opcode[3], not_5_out, Opcode[1], Opcode[0]);
  and andi (andi_out, not_2_out, not_1_out, Opcode[3], Opcode[2], not_4_out, not_8_out);
  and ori (ori_out, not_2_out, not_1_out, Opcode[3], Opcode[2], not_4_out, Opcode[0]);
  and Add (Add_out, ZeroOp_out, Funct[5], not_7_out, not_11_out, not_10_out, not_9_out, not_12_out);
  and Addi (Addi_out, not_2_out, not_1_out, Opcode[3], not_5_out, not_4_out, not_8_out);
  and And (And_out, ZeroOp_out, Funct[5], not_7_out, not_11_out, Funct[2], not_9_out, not_12_out);
  and Nor (Ainvert, ZeroOp_out, Funct[5], not_7_out, not_11_out, Funct[2], Funct[1], Funct[0]);
  and Or (Or_out, ZeroOp_out, Funct[5], not_7_out, not_11_out, Funct[2], not_9_out, Funct[0]);
  and Slt (Slt_out, ZeroOp_out, Funct[5], not_7_out, Funct[3], not_10_out, Funct[1], not_12_out);
  and Slti (Slti_out, not_2_out, not_1_out, Opcode[3], not_5_out, Opcode[1], not_8_out);
  and Sub (Sub_out, ZeroOp_out, Funct[5], not_7_out, not_11_out, not_10_out, Funct[1], not_12_out);
  and Subu (Subu_out, ZeroOp_out, Funct[5], not_6_out, not_7_out, not_10_out, Funct[1], Funct[0]);
  or u_Byte (Byte, lbu_out, sb_out);
  or u_Half (Half, lhu_out, sh_out);
  or u_Word (Word, lw_out, sw_out);
  or u_Shift (Shift, Sll_out, Sllv_out, lui, Srl_out, Srlv_out);
  or u_Shift_Direction (Shift_Direction, Srl_out, Srlv_out);
  or u_Shift_Value (Shift_Value, Sllv_out, lui, Srlv_out);
  or Zeroex (ZeroExtend, andi_out, lui, ori_out);
  or Binvt (Bnegate, Branch, Ainvert, Slt_out, bne, Slti_out, Sub_out, Subu_out);
  or u_RegShift (RegShift, Sll_out, Srl_out);
  or u_MemWrite (MemWrite, sb_out, sh_out, sw_out);
  or u_ALUSrc (ALUSrc, Opcode[5], Sll_out, Srl_out, Opcode[3]);
  not not_13 (not_13_out, lui);
  or Opbit0 (Operation[0], Or_out, ori_out, Slt_out, Slti_out);
  or u_MemRead (MemRead, lw_out, lbu_out, lhu_out);
  or Opbit1 (Operation[1], Add_out, Addi_out, Slt_out, Slti_out, Branch, bne, Sub_out, sw_out, sh_out, sb_out, MemRead, Subu_out);
  or u_RegWrite (RegWrite, Srlv_out, Sll_out, andi_out, Add_out, ori_out, Or_out, Addi_out, lw_out, Sub_out, Add_out, lui, Sllv_out, lhu_out, lbu_out, Subu_out, Ainvert, And_out, Slt_out, Slti_out, Srl_out, jal);

  assign MemtoReg = MemRead;
endmodule
